# Fritzing sketch PCBpedal (saved by Fritzing 0.8.7b)
circuit board: 5cm x 3.5cm
breadboards: 1

parts:
  U1 = atmega328 [package=dip]
  XTAL1 = Crystal [frequency="16 Mhz" package=THT]
  U2 = Voltage Regulator - 5V [package="TO220 [THT]"]
  J1 = female pin header, 5 pins [form="♀ (female)"]
  IC1 = MSGEQ7 [package=soic8]
  IC2 = MSGEQ7 [package=soic8]
  JP2 = Header 2 [package=molex-1x2_lock]
  JP3 = Header 3 [package=molex-1x3_lock]
  R4 = Resistor [tolerance=±5% resistance=10k package="1206 [SMD]"]
  C4 = Electrolytic Capacitor [capacitance=10µF package="1010 [SMD, electrolytic]"]
  C3 = Electrolytic Capacitor [capacitance=10µF package="1010 [SMD, electrolytic]"]
  C1 = Ceramic Capacitor [capacitance=22pF package="1206 [SMD, multilayer]"]
  C2 = Ceramic Capacitor [capacitance=22pF package="1206 [SMD, multilayer]"]
  C7 = Ceramic Capacitor [capacitance=0.1µF package="1206 [SMD, multilayer]"]
  C10 = Ceramic Capacitor [capacitance=0.1µF package="1206 [SMD, multilayer]"]
  C9 = Ceramic Capacitor [capacitance=0.1µF package="1206 [SMD, multilayer]"]
  C8 = Ceramic Capacitor [capacitance=33pF package="1206 [SMD, multilayer]"]
  C6 = Ceramic Capacitor [capacitance=0.1µF package="1206 [SMD, multilayer]"]
  C5 = Ceramic Capacitor [capacitance=33pF package="1206 [SMD, multilayer]"]
  R5 = Resistor [tolerance=±5% resistance=220 package="1206 [SMD]"]
  R3 = Resistor [tolerance=±5% resistance=200k package="1206 [SMD]"]
  R2 = Resistor [tolerance=±5% resistance=200k package="1206 [SMD]"]
  X1 = USB+SHIELD [package=usb-b-pth]
  JP4 = Header 6 [package=molex-1x6-ra]

nets:
  N1: U1.RESET, J1.pin3
  N2: U1.D0_(RX), J1.pin4
  N3: U1.D1_(TX), J1.pin5
  N4: U1.D2, R4.Pin_0, JP4.6
  N5: U1.D3_(PWM), X1.D-
  5V: U1.VCC, U1.AVCC, U1.AREF, U2.output_voltage, J1.pin1, IC1.VDD, IC2.VDD, JP2.2, C3.+, C7.0, C10.1, R5.Pin_1, R3.Pin_1, R2.Pin_1
  GND: U1.GND, U2.GND, J1.pin2, IC1.GND, IC2.GND, JP2.1, JP3.2, R4.Pin_1, C4.-, C3.-, C1.1, C2.1, C7.1, C10.0, C9.0, C8.0, C6.0, C5.0, X1.P$1, X1.P$2, X1.GND
  N6: U1.XLAT1, XTAL1.pin_1, C1.0
  N7: U1.XLAT2, XTAL1.pin_0, C2.0
  midi: U1.D6_(PWM), JP3.1
  N8: U1.D12, IC1.RESET, IC2.RESET
  N9: U1.D13, IC1.STROBE, IC2.STROBE
  N10: U1.A0, IC1.DCOUT
  N11: U1.A1, IC2.DCOUT
  N12: U1.A2, JP4.3
  N13: U1.A3, JP4.4
  N14: U1.A4, JP4.5
  N15: U2.input_voltage, C4.+, X1.VBUS
  N16: IC1.AUDIO_IN, JP4.1
  N17: IC1.CG, C9.1
  N18: IC1.CKIN, C8.1, R3.Pin_0
  N19: IC2.AUDIO_IN, JP4.2
  N20: IC2.CG, C6.1
  N21: IC2.CKIN, C5.1, R2.Pin_0
  N22: JP3.3, R5.Pin_0

notes:
  Gutar Pedal V1.
