# Fritzing sketch PCBpedalv2 (saved by Fritzing 0.8.7b)
circuit board: 5cm x 3.5cm
breadboards: 1

parts:
  IC1 = MSGEQ7 [package=soic8]
  IC2 = MSGEQ7 [package=soic8]
  IC3 = USB UART [package=ssop28db]
  U1 = USB+SHIELD [package=usb-b-pth]
  Atmega1 = ATmega328 [package=tqfp]
  XTAL1 = Crystal [frequency="16 Mhz" package=THT]
  C2 = Ceramic Capacitor [capacitance=22pF package="1206 [SMD, multilayer]"]
  C1 = Ceramic Capacitor [capacitance=22pF package="1206 [SMD, multilayer]"]
  C3 = Ceramic Capacitor [capacitance=0.1µF package="1206 [SMD, multilayer]"]
  C7 = Ceramic Capacitor [capacitance=33pF package="1206 [SMD, multilayer]"]
  C4 = Ceramic Capacitor [capacitance=0.1µF package="1206 [SMD, multilayer]"]
  C6 = Ceramic Capacitor [capacitance=33pF package="1206 [SMD, multilayer]"]
  C8 = Ceramic Capacitor [capacitance=0.1µF package="1206 [SMD, multilayer]"]
  C9 = Ceramic Capacitor [capacitance=0.1µF package="1206 [SMD, multilayer]"]
  R1 = Resistor [tolerance=±5% resistance=200k package="1206 [SMD]"]
  R2 = Resistor [tolerance=±5% resistance=200k package="1206 [SMD]"]
  J3 = female pin header, 6 pins [form="♀ (female)"]
  J4 = female pin header, 2 pins [form="♀ (female)"]
  D1 = Rectifier Diode [part_number=1n914 package="Melf DO-213 AA [SMD]"]
  R4 = Resistor [tolerance=±5% resistance=220 package="1206 [SMD]"]
  R5 = Resistor [tolerance=±5% resistance=270 package="1206 [SMD]"]
  C13 = Electrolytic Capacitor [capacitance=10µF package="0605 [SMD, electrolytic]"]
  C14 = Electrolytic Capacitor [capacitance=10µF package="0605 [SMD, electrolytic]"]
  C15 = Ceramic Capacitor [capacitance=1nF package="1206 [SMD, multilayer]"]
  C16 = Ceramic Capacitor [capacitance=1nF package="1206 [SMD, multilayer]"]
  R3 = Resistor [tolerance=±5% resistance=220 package="1206 [SMD]"]
  U2 = OPTO_DARL_6N138S [package=8-smd]
  C11 = Electrolytic Capacitor [capacitance=10µF package="0605 [SMD, electrolytic]"]
  C10 = Ceramic Capacitor [capacitance=0.1µF package="1206 [SMD, multilayer]"]
  C12 = Ceramic Capacitor [capacitance=0.1µF package="1206 [SMD, multilayer]"]
  IC5 = Voltage Regulator LM1117 [package=sot223]
  J5 = female pin header, 2 pins [form="♀ (female)"]

nets:
  5V: IC1.VDD, IC2.VDD, IC3.VCC, U1.VBUS, Atmega1.VCC, Atmega1.AVCC, Atmega1.AREF, C8.0, C9.0, R1.Pin_1, R2.Pin_1, R5.Pin_0, C13.+, U2.VCC, C11.+, C10.1, IC5.OUT
  GND: IC1.GND, IC2.GND, IC3.GND7, IC3.GND18, IC3.GND21, IC3.AGND, IC3.TEST, U1.P$1, U1.P$2, U1.GND, Atmega1.GND, Atmega1.AGND, C2.1, C1.1, C3.0, C7.0, C4.0, C6.0, C8.1, C9.1, C13.-, C14.-, R3.Pin_1, U2.GND, C11.-, C10.0, C12.0, IC5.ADJ, J5.pin1
  N1: IC1.DCOUT, Atmega1.PC0(ADC0)
  N2: IC1.STROBE, IC2.STROBE, Atmega1.PB5(SCK)
  N3: IC1.AUDIO_IN, C15.0
  N4: IC1.CG, C3.1
  N5: IC1.RESET, IC2.RESET, Atmega1.PB4(MISO)
  N6: IC1.CKIN, C7.1, R2.Pin_0
  N7: IC2.DCOUT, Atmega1.PC1(ADC1)
  N8: IC2.AUDIO_IN, C16.0
  N9: IC2.CG, C4.1
  N10: IC2.CKIN, C6.1, R1.Pin_0
  N11: IC3.TXD, Atmega1.PD0(RXD)
  N12: IC3.RXD, Atmega1.PD1(TXD)
  N13: IC3.USBDP, U1.D+
  N14: IC3.USBDM, U1.D-
  N15: IC3.3V3OUT, C12.1
  N16: Atmega1.PB6(XTAL1_TOSC1), XTAL1.pin_1, C1.0
  N17: Atmega1.PB7(XTAL2_TOSC2), XTAL1.pin_0, C2.0
  N18: Atmega1.PB3(MOSI_OC2), R5.Pin_1, U2.VOUT
  N19: Atmega1.PC2(ADC2), J3.pin3
  N20: Atmega1.PC3(ADC3), J3.pin4
  N21: Atmega1.PC4(ADC4_SDA), J3.pin5
  N22: Atmega1.PD2(INT0), J3.pin6, R3.Pin_0
  N23: J3.pin1, C15.1
  N24: J3.pin2, C16.1
  N25: J4.pin1, D1.anode, U2.C
  N26: J4.pin2, R4.Pin_0
  N27: D1.cathode, R4.Pin_1, U2.A
  N28: C14.+, IC5.IN, J5.pin2

notes:
  Guitar Pedal V2.
