# Fritzing sketch gpedalkitv1 (saved by Fritzing 0.8.7b)
circuit board: 6.16844cm x 4.79705cm
breadboards: 1

parts:
  FTDI_BREAKOUT = FTDI Basic Programmer
  ATMEGA328P-PU = atmega328 [package=dip]
  msgeq7 = DIP - 8 pins [chip_label=MSGEQ7 package="DIP (Dual Inline) [THT]"]
  J4 = female pin header, 6 pins [form="♀ (female)"]
  msgeq7_2 = DIP - 8 pins [chip_label=MSGEQ7 package="DIP (Dual Inline) [THT]"]
  XTAL2 = Crystal [frequency="16 Mhz" package=THT]
  J6 = female pin header, 2 pins [form="♀ (female)"]
  LM7805 = Voltage Regulator - 5V [package="TO220 [THT]"]
  J7 = female pin header, 3 pins [form="♀ (female)"]
  R5 = Resistor [tolerance=±5% resistance=220 package=THT]
  R3 = Resistor [tolerance=±5% resistance=200k package=THT]
  R4 = Resistor [tolerance=±5% resistance=200k package=THT]
  C22 = Ceramic Capacitor [capacitance=22pF package="200 mil [THT, multilayer]"]
  C23 = Ceramic Capacitor [capacitance=22pF package="200 mil [THT, multilayer]"]
  C24 = Electrolytic Capacitor [capacitance=10µF package="200 mil [THT, electrolytic]"]
  C25 = Electrolytic Capacitor [capacitance=10µF package="200 mil [THT, electrolytic]"]
  C19 = Ceramic Capacitor [capacitance=0.1µF package="200 mil [THT, multilayer]"]
  C18 = Ceramic Capacitor [capacitance=33pF package="200 mil [THT, multilayer]"]
  C8 = Ceramic Capacitor [capacitance=33pF package="200 mil [THT, multilayer]"]
  C9 = Ceramic Capacitor [capacitance=0.1µF package="200 mil [THT, multilayer]"]
  C16 = Ceramic Capacitor [capacitance=1nF package="200 mil [THT, multilayer]"]
  C20 = Ceramic Capacitor [capacitance=1nF package="200 mil [THT, multilayer]"]
  C21 = Ceramic Capacitor [capacitance=0.1µF package="200 mil [THT, multilayer]"]
  C17 = Ceramic Capacitor [capacitance=0.1µF package="200 mil [THT, multilayer]"]

nets:
  N1: FTDI_BREAKOUT.RXI, ATMEGA328P-PU.D1_(TX)
  N2: FTDI_BREAKOUT.TXO, ATMEGA328P-PU.D0_(RX)
  5V: FTDI_BREAKOUT.POWER, ATMEGA328P-PU.VCC, msgeq7.VDD, msgeq7_2.VDD, LM7805.output_voltage, R3.Pin_1, R4.Pin_1, C25.+, C21.0, C17.0
  GND: FTDI_BREAKOUT.GND, ATMEGA328P-PU.GND, msgeq7.GND, msgeq7_2.GND, J6.pin1, LM7805.GND, J7.pin3, R5.Pin_1, C22.1, C23.1, C24.-, C25.-, C19.0, C18.0, C8.0, C9.0, C21.1, C17.1
  N3: ATMEGA328P-PU.D3_(PWM), J7.pin2
  N4: ATMEGA328P-PU.XLAT1, XTAL2.pin_1, C22.0
  N5: ATMEGA328P-PU.XLAT2, XTAL2.pin_0, C23.0
  N6: ATMEGA328P-PU.D7, J4.pin6, R5.Pin_0
  N7: ATMEGA328P-PU.D12, msgeq7.RESET, msgeq7_2.RESET
  N8: ATMEGA328P-PU.D13, msgeq7.STROBE, msgeq7_2.STROBE
  N9: ATMEGA328P-PU.A0, msgeq7_2.DCOUT
  N10: ATMEGA328P-PU.A1, msgeq7.DCOUT
  N11: ATMEGA328P-PU.A2, J4.pin3
  N12: ATMEGA328P-PU.A3, J4.pin4
  N13: ATMEGA328P-PU.A4, J4.pin5
  N14: msgeq7.AUDIO_IN, C16.1
  N15: msgeq7.CG, C9.1
  N16: msgeq7.CKIN, R3.Pin_0, C8.1
  N17: J4.pin1, C16.0
  N18: J4.pin2, C20.0
  N19: msgeq7_2.AUDIO_IN, C20.1
  N20: msgeq7_2.CG, C19.1
  N21: msgeq7_2.CKIN, R4.Pin_0, C18.1
  N22: J6.pin2, LM7805.input_voltage, J7.pin1, C24.+

custom parts:
  DIP - 8 pins: A DIP stand-in part for whatever IC you want. With 8 pins on a 300mil dual inline package (DIP) footprint.
