# Fritzing sketch PCBpedalv3 (saved by Fritzing 0.8.7b)
circuit board: 5cm x 3.5cm
breadboards: 1

parts:
  IC1 = MSGEQ7 [package=soic8]
  IC2 = MSGEQ7 [package=soic8]
  ft232 = USB UART [package=ssop28db]
  U1 = USB+SHIELD [package=usb-b-pth]
  atmega = ATmega328 [package=tqfp]
  C2 = Ceramic Capacitor [capacitance=22pF package="1206 [SMD, multilayer]"]
  C3 = Ceramic Capacitor [capacitance=0.1µF package="1206 [SMD, multilayer]"]
  C7 = Ceramic Capacitor [capacitance=33pF package="1206 [SMD, multilayer]"]
  C4 = Ceramic Capacitor [capacitance=0.1µF package="1206 [SMD, multilayer]"]
  C6 = Ceramic Capacitor [capacitance=33pF package="1206 [SMD, multilayer]"]
  C8 = Ceramic Capacitor [capacitance=0.1µF package="1206 [SMD, multilayer]"]
  C9 = Ceramic Capacitor [capacitance=0.1µF package="1206 [SMD, multilayer]"]
  R1 = Resistor [tolerance=±5% resistance=200k package="1206 [SMD]"]
  R2 = Resistor [tolerance=±5% resistance=200k package="1206 [SMD]"]
  C15 = Ceramic Capacitor [capacitance=1nF package="1206 [SMD, multilayer]"]
  C16 = Ceramic Capacitor [capacitance=1nF package="1206 [SMD, multilayer]"]
  R3 = Resistor [tolerance=±5% resistance=220 package="1206 [SMD]"]
  C10 = Ceramic Capacitor [capacitance=0.1µF package="1206 [SMD, multilayer]"]
  C12 = Ceramic Capacitor [capacitance=0.1µF package="1206 [SMD, multilayer]"]
  IC5 = Voltage Regulator LM1117 [package=sot223]
  PWR = female pin header, 2 pins [form="♀ (female)"]
  R4 = Resistor [tolerance=±5% resistance=10k package="1206 [SMD]"]
  R5 = Resistor [tolerance=±5% resistance=1M package="1206 [SMD]"]
  C17 = Ceramic Capacitor [capacitance=100nF package="1206 [SMD, multilayer]"]
  C19 = Ceramic Capacitor [capacitance=10nF package="1206 [SMD, multilayer]"]
  ISCP = AVR ISP 6 Pin [package=2x3-ns]
  XTAL1 = Crystal [frequency="16 Mhz" package=THT]
  J3 = female pin header, 7 pins [form="♀ (female)"]
  C11 = Electrolytic Capacitor [capacitance=10µF package="0405 [SMD, electrolytic]"]
  C13 = Electrolytic Capacitor [capacitance=10µF package="0405 [SMD, electrolytic]"]
  C14 = Electrolytic Capacitor [capacitance=10µF package="0405 [SMD, electrolytic]"]
  C18 = Electrolytic Capacitor [capacitance=10µF package="0405 [SMD, electrolytic]"]
  C1 = Ceramic Capacitor [capacitance=22pF package="1206 [SMD, multilayer]"]
  NO = smd LED [color="Red (633nm)" package="1206 [SMD]"]
  R6 = Resistor [tolerance=±5% resistance=1k package="1206 [SMD]"]
  J6 = female pin header, 3 pins [form="♀ (female)"]
  LED = female pin header, 2 pins [form="♀ (female)"]

nets:
  5V: IC1.VDD, IC2.VDD, ft232.VCC, U1.VBUS, atmega.VCC, atmega.AVCC, atmega.AREF, C8.0, C9.0, R1.Pin_1, R2.Pin_1, C10.1, IC5.OUT, R4.Pin_0, C19.1, ISCP.2, C11.+, C13.+, NO.anode, J6.pin1
  GND: IC1.GND, IC2.GND, ft232.GND7, ft232.GND18, ft232.GND21, ft232.AGND, ft232.TEST, U1.P$1, U1.P$2, U1.GND, atmega.GND, atmega.AGND, C2.1, C3.0, C7.0, C4.0, C6.0, C8.1, C9.1, R3.Pin_1, C10.0, C12.0, IC5.ADJ, PWR.pin1, C19.0, ISCP.6, C11.-, C13.-, C14.-, C1.1, R6.Pin_0, LED.pin1
  N1: IC1.DCOUT, atmega.PC0(ADC0)
  N2: IC1.STROBE, IC2.STROBE, atmega.PB4(MISO), ISCP.1
  N3: IC1.AUDIO_IN, C15.0
  N4: IC1.CG, C3.1
  N5: IC1.RESET, IC2.RESET, atmega.PB5(SCK), ISCP.3
  N6: IC1.CKIN, C7.1, R2.Pin_0
  N7: IC2.DCOUT, atmega.PC1(ADC1)
  N8: IC2.AUDIO_IN, C16.0
  N9: IC2.CG, C4.1
  N10: IC2.CKIN, C6.1, R1.Pin_0
  N11: ft232.TXD, atmega.PD0(RXD)
  N12: ft232.DTR, R5.Pin_0, C18.-
  N13: ft232.RXD, atmega.PD1(TXD)
  N14: ft232.CTS, C17.1
  N15: ft232.USBDP, U1.D+
  N16: ft232.USBDM, U1.D-
  N17: ft232.3V3OUT, C12.1
  N18: atmega.PB6(XTAL1_TOSC1), XTAL1.pin_1, C1.0
  N19: atmega.PB7(XTAL2_TOSC2), C2.0, XTAL1.pin_0
  N20: atmega.PD5(T1), R3.Pin_0, J3.pin7
  N21: atmega.PD6(AIN0), J3.pin6
  N22: atmega.PB3(MOSI_OC2), ISCP.4
  N23: atmega.PC2(ADC2), J3.pin3
  N24: atmega.PC3(ADC3), J3.pin4
  N25: atmega.PC4(ADC4_SDA), J3.pin5
  N26: atmega.PC6(_RESET), R4.Pin_1, R5.Pin_1, C17.0, ISCP.5, C18.+
  N27: C15.1, J3.pin1
  N28: C16.1, J3.pin2
  N29: IC5.IN, PWR.pin2, C14.+, J6.pin3
  N30: NO.cathode, R6.Pin_1
  N31: J6.pin2, LED.pin2

notes:
  Guitar Pedal V3.
